# Fritzing sketch schematic (saved by Fritzing 0.9.3b)
breadboards: 1

parts:
  Componente1 = Arduino Due (Rev2b)
  J1 = female pin header, 7 pins [form="♀ (female)"]
  J2 = Camdenboss CTB0158-2 [part_number=CTB0158-2 package=THT]
  J3 = Camdenboss CTB0158-2 [part_number=CTB0158-2 package=THT]  # not connected
  J4 = Camdenboss CTB0158-2 [part_number=CTB0158-2 package=THT]  # not connected
  J5 = Camdenboss CTB0158-2 [part_number=CTB0158-2 package=THT]  # not connected
  L1 = Inductor [package="1206 [SMD]"]
  R1 = Resistor [tolerance=±5% resistance=4.7k package=THT]
  R2 = Resistor [tolerance=±5% resistance=4.7k package=THT]

nets:
  N1: Componente1.IOREF, J1.pin1, R1.Pin_1, R2.Pin_1
  N2: Componente1.GND, J1.pin2, J1.pin4, J1.pin5
  N3: Componente1.SDA1, J1.pin6, R2.Pin_0
  N4: Componente1.SCL1, J1.pin7, R1.Pin_0
  N5: Componente1.D2_PWM, J1.pin3
  N6: J2.pin1, L1.pin_0
  N7: J2.pin2, L1.pin_1

notes:
  3V3
  GND
  INTB
  SD
  ADDR
  SDA
  SCL
  LDC16xx
  4k7
